# Fritzing sketch Gyro-Box (saved by Fritzing 0.9.5d)
breadboards: 1

parts:
  Bauteil11 = Arduino Uno (Rev3) - ICSP
  Bauteil15 = InvenSense MPU6050
  LED1 = LED - 5mm [color="White (4500K)" package="5 mm [THT]"]
  LED2 = LED - 5mm [color="White (4500K)" package="5 mm [THT]"]
  LED3 = LED - 5mm [color="White (4500K)" package="5 mm [THT]"]
  LED4 = LED - 5mm [color="White (4500K)" package="5 mm [THT]"]
  HC-SR04_Sensor_1 = HC-SR04 Ultrasonic Distance Sensor

nets:
  N1: Bauteil11.A4/SDA, Bauteil15.SDA
  N2: Bauteil11.A5/SCL, Bauteil15.SCL
  N3: Bauteil11.D8, LED2.anode
  N4: Bauteil11.D9_PWM, LED1.anode
  N5: Bauteil11.D10_PWM/SS, LED4.anode
  N6: Bauteil11.D11_PWM/MOSI, LED3.anode
  GND: Bauteil11.GND, Bauteil15.GND, LED1.cathode, LED2.cathode, LED3.cathode, LED4.cathode, HC-SR04_Sensor_1.GND
  N7: Bauteil11.D2, HC-SR04_Sensor_1.TRIG
  N8: Bauteil11.D3_PWM, HC-SR04_Sensor_1.ECHO
  VCC: Bauteil11.5V, Bauteil15.VCC, HC-SR04_Sensor_1.VCC
