# Fritzing sketch motor-pipe-sensor (saved by Fritzing 0.9.5d)
breadboards: 1

parts:
  Bauteil1 = Arduino Uno (Rev3)
  HC-SR04_Sensor_1 = HC-SR04 Ultrasonic Distance Sensor
  DFRobot_DFPlayer_Mini1 = DFRobot DFPlayer Mini [part_number=DFR0299]
  R1 = Resistor [tolerance=±5% resistance=1000 package=THT]
  SPKR1 = Loudspeaker
  Driver1 = 28BYJ-48 Driver Module [part_number=ULN2003 package=THT]
  SM1 = 28BYJ-48 Stepper Motor [part_number=28BYJ-48]  # not connected
  Bauteil2 = Arduino Uno (Rev3)
  Bauteil3 = Arduino Uno (Rev3)
  Driver2 = 28BYJ-48 Driver Module [part_number=ULN2003 package=THT]
  SM2 = 28BYJ-48 Stepper Motor [part_number=28BYJ-48]  # not connected
  Bauteil4 = Arduino Uno (Rev3)
  Driver3 = 28BYJ-48 Driver Module [part_number=ULN2003 package=THT]
  SM3 = 28BYJ-48 Stepper Motor [part_number=28BYJ-48]  # not connected

nets:
  N1: Bauteil1.A0, HC-SR04_Sensor_1.TRIG
  N2: Bauteil1.A1, HC-SR04_Sensor_1.ECHO
  N3: Bauteil1.D8, Bauteil2.A0
  N4: Bauteil1.D10_PWM/SS, DFRobot_DFPlayer_Mini1.TX
  N5: Bauteil1.D11_PWM/MOSI, R1.Pin_1
  GND: Bauteil1.GND, HC-SR04_Sensor_1.GND, DFRobot_DFPlayer_Mini1.GND-1, DFRobot_DFPlayer_Mini1.GND-2, Driver1.GND, Bauteil2.GND, Bauteil3.GND, Driver2.GND, Bauteil4.GND, Driver3.GND
  VCC: Bauteil1.5V, HC-SR04_Sensor_1.VCC, DFRobot_DFPlayer_Mini1.VCC
  N6: DFRobot_DFPlayer_Mini1.RX, R1.Pin_0
  N7: DFRobot_DFPlayer_Mini1.SPK_1, SPKR1.pin2
  N8: Driver1.IN1, Bauteil2.D2
  N9: Driver1.IN2, Bauteil2.D3_PWM
  N10: Driver1.IN3, Bauteil2.D4
  N11: Driver1.IN4, Bauteil2.D5_PWM
  N12: Driver1.Vmotor, Bauteil2.5V
  N13: Bauteil2.D8, Bauteil3.A0
  N14: Bauteil3.D8, Bauteil4.A0
  N15: Bauteil3.D2, Driver2.IN1
  N16: Bauteil3.D3_PWM, Driver2.IN2
  N17: Bauteil3.D4, Driver2.IN3
  N18: Bauteil3.D5_PWM, Driver2.IN4
  N19: Bauteil3.5V, Driver2.Vmotor
  N20: Bauteil4.D2, Driver3.IN1
  N21: Bauteil4.D3_PWM, Driver3.IN2
  N22: Bauteil4.D4, Driver3.IN3
  N23: Bauteil4.D5_PWM, Driver3.IN4
  N24: Bauteil4.5V, Driver3.Vmotor

notes:
  One Door Module
  Three Motor Modules

custom parts:
  28BYJ-48 Driver Module: ULN2003 Driver Module for the 28BYJ-48 Unipolar Stepper Motor LED A - Blue wire - Bottom coil left LED B - Pink wire - Top coil left LED C - Yellow wire - Bottom coil right LED D - Orange wire - Top coil right Common rail - red Connector pins: blue - pink - yellow - orange - red Control pins - IN1 to IN4 Power pins - GND & Vmotor (5-12V) On/Off jumper (if removed, power to motor is cut).
  28BYJ-48 Stepper Motor: Unipolar Stepper Motor 28BYJ-48 Top coil - pink & orange Bottom coil - blue & yellow Common rail - red Connector pins: blue - pink - yellow - orange - red
