# Fritzing sketch ToF-Projector (saved by Fritzing 0.9.5d)
breadboards: 1

parts:
  Bauteil1 = Adafruit VL53L1X [part_number="Adafruit #3967"]
  Bauteil2 = Arduino Uno (Rev3) - ICSP
  Bauteil3 = Arduino Uno (Rev3) - ICSP
  Bauteil4 = Adafruit VL53L1X [part_number="Adafruit #3967"]
  Bauteil5 = Arduino Uno (Rev3) - ICSP
  Bauteil8 = Adafruit VL53L1X [part_number="Adafruit #3967"]
  Bauteil9 = Arduino Uno (Rev3) - ICSP
  Bauteil11 = Arduino Uno (Rev3) - ICSP
  Bauteil12 = Adafruit VL53L1X [part_number="Adafruit #3967"]
  Bauteil14 = Adafruit VL53L1X [part_number="Adafruit #3967"]
  DFRobot_DFPlayer_Mini2 = DFRobot DFPlayer Mini [part_number=DFR0299]
  R2 = Resistor [tolerance=±5% resistance=1000 package=THT]
  SPKR2 = Loudspeaker

nets:
  VCC: Bauteil1.VCC, Bauteil2.5V
  N1: Bauteil1.SDA, Bauteil2.A4/SDA
  N2: Bauteil1.SCL, Bauteil2.A5/SCL
  GND: Bauteil1.GND, Bauteil2.GND
  N3: Bauteil2.A0, Bauteil5.D8
  N4: Bauteil2.A1, Bauteil5.D9_PWM
  N5: Bauteil2.A2, Bauteil5.D10_PWM/SS
  N6: Bauteil2.D8, Bauteil3.A0
  N7: Bauteil2.D9_PWM, Bauteil3.A1
  N8: Bauteil2.D10_PWM/SS, Bauteil3.A2
  N9: Bauteil2.D11_PWM/MOSI, Bauteil3.A3
  N10: Bauteil3.A4/SDA, Bauteil4.SDA
  N11: Bauteil3.A5/SCL, Bauteil4.SCL
  N12: Bauteil3.D10_PWM/SS, DFRobot_DFPlayer_Mini2.TX
  N13: Bauteil3.D11_PWM/MOSI, R2.Pin_1
  VCC_2: Bauteil3.5V, Bauteil4.VCC, DFRobot_DFPlayer_Mini2.VCC
  GND_2: Bauteil3.GND, Bauteil4.GND, DFRobot_DFPlayer_Mini2.GND-1, DFRobot_DFPlayer_Mini2.GND-2
  N14: Bauteil5.A0, Bauteil9.D8
  N15: Bauteil5.A1, Bauteil9.D9_PWM
  N16: Bauteil5.A4/SDA, Bauteil8.SDA
  N17: Bauteil5.A5/SCL, Bauteil8.SCL
  GND_3: Bauteil5.GND, Bauteil8.GND
  5V: Bauteil5.5V, Bauteil8.VCC
  N18: Bauteil9.A0, Bauteil11.D8
  N19: Bauteil9.A4/SDA, Bauteil12.SDA
  N20: Bauteil9.A5/SCL, Bauteil12.SCL
  GND_4: Bauteil9.GND, Bauteil12.GND
  5V_2: Bauteil9.5V, Bauteil12.VCC
  N21: Bauteil11.A4/SDA, Bauteil14.SDA
  N22: Bauteil11.A5/SCL, Bauteil14.SCL
  GND_5: Bauteil11.GND, Bauteil14.GND
  5V_3: Bauteil11.5V, Bauteil14.VCC
  N23: DFRobot_DFPlayer_Mini2.RX, R2.Pin_0
  N24: DFRobot_DFPlayer_Mini2.SPK_1, SPKR2.pin2

notes:
  One Projector Module
  Four Sensor Modules

custom parts:
  Adafruit VL53L1X: The Adafruit VL53L1X Time of Flight Distance Sensor (also known as VL53L1CX) is a Time of Flight distance sensor that has a massive 4 meter range and LIDAR-like precision. The sensor contains a very tiny invisible laser source and a matching sensor. The VL53L1X can detect the "time of flight", or how long the light has taken to bounce back to the sensor. Since it uses a very narrow light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
