# Fritzing sketch knock-textiles (saved by Fritzing 0.9.5d)
breadboards: 1

parts:
  Bauteil1 = Arduino Uno (Rev3)
  DFRobot_DFPlayer_Mini1 = DFRobot DFPlayer Mini [part_number=DFR0299]
  R1 = Resistor [tolerance=±5% resistance=1000 package=THT]
  SPKR1 = Loudspeaker
  Mod1 = KY-002 Vibration Switch Module [package="Breakout board"]
  Mod2 = KY-002 Vibration Switch Module [package="Breakout board"]

nets:
  N1: Bauteil1.D8, Mod1.S
  N2: Bauteil1.D10_PWM/SS, DFRobot_DFPlayer_Mini1.TX
  N3: Bauteil1.D11_PWM/MOSI, R1.Pin_1
  N4: Bauteil1.GND, DFRobot_DFPlayer_Mini1.GND-1, DFRobot_DFPlayer_Mini1.GND-2, Mod1.-, Mod2.-
  N5: Bauteil1.D7, Mod2.S
  VIN: Bauteil1.3V3, Mod1.Vin, Mod2.Vin
  5V: Bauteil1.5V, DFRobot_DFPlayer_Mini1.VCC
  N6: DFRobot_DFPlayer_Mini1.RX, R1.Pin_0
  N7: DFRobot_DFPlayer_Mini1.SPK_1, SPKR1.pin2

custom parts:
  KY-002 Vibration Switch Module: Arduino Vibration Switch Module KY-002 Keyes allows detection of shock and vibration.
